# Fritzing sketch Untitled Sketch (saved by Fritzing 0.9.3b)

parts:
  U1 = ESP32-38PinWide [part_number=ESP32-38PinWide]
  S1 = H-Bridge with L298N
  M1 = DC Motor
  M2 = DC Motor
  U2 = LIPO-2000mAh [package=lipo-2000]
  U3 = LIPO-2000mAh [package=lipo-2000]
  M3 = fc-51 [package=THT]
  M5 = fc-51 [package=THT]
  M6 = fc-51 [package=THT]
  M7 = fc-51 [package=THT]
  M8 = fc-51 [package=THT]

nets:
  N1: U1.GPIO26, S1.IN4
  N2: U1.GPIO27, S1.IN3
  N3: U1.GPIO12, S1.IN2
  N4: U1.GPIO13, S1.IN1
  N5: U1.GPIO11, S1.GND, U2.-, M5.pin1
  VIN: U1.VIN, S1.5V, M3.pin3
  N6: U1.GPIO4, M3.pin2
  N7: U1.GPIO16, M8.pin2
  N8: U1.GPIO17, M7.pin2
  N9: U1.GPIO5, M6.pin2
  N10: U1.GPIO18, M5.pin2
  N11: S1.12V, U3.+
  N12: S1.ENA, S1.ENA-5V
  N13: S1.ENB, S1.ENB-5V
  N14: S1.M1-01, M2.pin_2
  N15: S1.M1-02, M2.pin_1
  N16: S1.M2-01, M1.pin_2
  N17: S1.M2-02, M1.pin_1
  N18: U2.+, U3.-

custom parts:
  ESP32-38PinWide: Generic 38-Pin ESP32 with wide format (only access to one side of pins on a breadboard) based on Stephen Lilley's HiLetgo ESP-WROOM-32 ESP32 ESP-32S Development Board.
  H-Bridge with L298N: h-bridge
