# Fritzing sketch dieukhien (saved by Fritzing 0.9.3b)

parts:
  Part1 = Arduino Uno (Rev3) - ICSP  # not connected
  U1 = LIPO-2000mAh [package=lipo-2000]
  U2 = LIPO-2000mAh [package=lipo-2000]
  U3 = LIPO-2000mAh [package=lipo-2000]
  S1 = H-Bridge with L298N
  M1 = DC Motor
  M2 = DC Motor
  M3 = DC Motor
  M4 = DC Motor
  M5 = RioRand LM2596

nets:
  N1: U1.+, M5.Pin_1
  N2: U1.-, U2.+
  N3: U2.-, U3.+
  N4: S1.M1-01, M3.pin_2, M4.pin_2
  N5: S1.M1-02, M3.pin_1, M4.pin_1
  N6: S1.M2-01, M1.pin_2, M2.pin_2
  N7: S1.M2-02, M1.pin_1, M2.pin_1

custom parts:
  H-Bridge with L298N: h-bridge
